# Fritzing sketch Ultrasonic-Buzzer (saved by Fritzing 0.9.3b)
breadboards: 1

parts:
  元件1 = LinkIt 7697
  Part3 = SRF05 Ultrasonic Rangefinder
  J1 = Piezo Speaker
  R1 = Resistor [tolerance=±5% resistance=220 package=THT]

nets:
  N1: 元件1.P2, Part3.Trig
  N2: 元件1.P3, Part3.Echo
  N3: 元件1.P16, 元件1.RTC_PWR_POS
  GND: 元件1.GND, 元件1.RTC_PWR_NEG, Part3.GND, J1.pin1
  3V3: 元件1.3V3, Part3.VCC
  N4: J1.pin2, R1.Pin_0

custom parts:
  LinkIt 7697: LinkIt 7697 is an IoT development board based on MT7697, supporting Wi-Fi and Bluetooth Low Energy connectivity.
