# Fritzing sketch Ultrasonic-LED (saved by Fritzing 0.9.3b)
breadboards: 1

parts:
  元件1 = LinkIt 7697
  LED1 = smd LED [color="Red (633nm)" package="0805 [SMD]"]
  R1 = Resistor [tolerance=±5% resistance=220 package=THT]
  Part3 = SRF05 Ultrasonic Rangefinder

nets:
  N1: 元件1.P2, Part3.Trig
  N2: 元件1.P3, Part3.Echo
  N3: 元件1.P4, R1.Pin_0
  GND: 元件1.GND, 元件1.RTC_PWR_NEG, LED1.cathode, Part3.GND
  3V3: 元件1.3V3, Part3.VCC
  N4: LED1.anode, R1.Pin_1

custom parts:
  LinkIt 7697: LinkIt 7697 is an IoT development board based on MT7697, supporting Wi-Fi and Bluetooth Low Energy connectivity.
