# Fritzing sketch buzzer (saved by Fritzing 0.9.3b)
breadboards: 1

parts:
  元件1 = LinkIt 7697
  R1 = Resistor [tolerance=±5% resistance=220 package=THT]
  SPKR1 = Loudspeaker

nets:
  N1: 元件1.P3, R1.Pin_1
  N2: 元件1.P16, 元件1.RTC_PWR_POS
  N3: 元件1.GND, SPKR1.pin1
  N4: R1.Pin_0, SPKR1.pin2

custom parts:
  LinkIt 7697: LinkIt 7697 is an IoT development board based on MT7697, supporting Wi-Fi and Bluetooth Low Energy connectivity.
