# Fritzing sketch dht (saved by Fritzing 0.9.3b)
breadboards: 1

parts:
  元件1 = LinkIt 7697

nets:
  N1: 元件1.P16, 元件1.RTC_PWR_POS

custom parts:
  LinkIt 7697: LinkIt 7697 is an IoT development board based on MT7697, supporting Wi-Fi and Bluetooth Low Energy connectivity.
