# Fritzing sketch led (saved by Fritzing 0.9.3b)
breadboards: 1

parts:
  元件1 = LinkIt 7697
  LED1 = smd LED [color="Red (633nm)" package="0805 [SMD]"]
  R1 = Resistor [tolerance=±5% resistance=220 package=THT]

nets:
  N1: 元件1.P2, R1.Pin_0
  N2: 元件1.P16, 元件1.RTC_PWR_POS
  N3: 元件1.GND, LED1.cathode
  N4: LED1.anode, R1.Pin_1

custom parts:
  LinkIt 7697: LinkIt 7697 is an IoT development board based on MT7697, supporting Wi-Fi and Bluetooth Low Energy connectivity.
